# Fritzing sketch nightrider (saved by Fritzing 0.9.9b)
breadboards: 1

parts:
  LED1 = LED - 5mm [color="Green (565nm)" current=0.030 package="5 mm [THT]"]
  LED2 = LED - 5mm [color="Yellow (592nm)" current=0.030 package="5 mm [THT]"]
  LED3 = LED - 5mm [color="Red (633nm)" current=0.030 package="5 mm [THT]"]
  LED8 = LED - 5mm [color="Red (633nm)" current=0.030 package="5 mm [THT]"]
  R1 = Resistor [tolerance=±5% power=0.25 resistance=220 package=THT]
  R2 = Resistor [tolerance=±5% power=0.25 resistance=220 package=THT]
  R3 = Resistor [tolerance=±5% power=0.25 resistance=220 package=THT]
  R4 = Resistor [tolerance=±5% power=0.25 resistance=220 package=THT]
  R5 = Resistor [tolerance=±5% power=0.25 resistance=220 package=THT]
  R6 = Resistor [tolerance=±5% power=0.25 resistance=220 package=THT]
  R7 = Resistor [tolerance=±5% power=0.25 resistance=220 package=THT]
  R8 = Resistor [tolerance=±5% power=0.25 resistance=220 package=THT]
  S1 = Pushbutton [package="[THT]"]
  S2 = Pushbutton [package="[THT]"]
  S3 = Pushbutton [package="[THT]"]
  S4 = Pushbutton [package="[THT]"]
  Bauteil1 = Arduino Uno (Rev3) - ICSP
  LED9 = LED - 5mm [color="Green (565nm)" current=0.030 package="5 mm [THT]"]
  LED10 = LED - 5mm [color="Yellow (592nm)" current=0.030 package="5 mm [THT]"]
  LED11 = LED - 5mm [color="Yellow (592nm)" current=0.030 package="5 mm [THT]"]
  LED12 = LED - 5mm [color="Green (565nm)" current=0.030 package="5 mm [THT]"]
  R9 = Resistor [tolerance=±5% power=0.25 resistance=10000 package=THT]
  R10 = Resistor [tolerance=±5% power=0.25 resistance=10000 package=THT]
  R11 = Resistor [tolerance=±5% power=0.25 resistance=10000 package=THT]
  R12 = Resistor [tolerance=±5% power=0.25 resistance=10000 package=THT]

nets:
  N1: LED1.cathode, R1.Pin_1
  N2: LED1.anode, Bauteil1.D9_PWM
  N3: LED2.cathode, R2.Pin_1
  N4: LED2.anode, Bauteil1.D8
  N5: LED3.cathode, R3.Pin_1
  N6: LED3.anode, Bauteil1.D7
  N7: LED8.cathode, R6.Pin_1
  N8: LED8.anode, Bauteil1.D4
  N9: R1.Pin_0, R2.Pin_0, R3.Pin_0, R4.Pin_0, R5.Pin_0, R6.Pin_0, R7.Pin_0, R8.Pin_0, Bauteil1.GND, R9.Pin_1, R10.Pin_1, R11.Pin_1, R12.Pin_1
  N10: R4.Pin_1, LED9.cathode
  N11: R5.Pin_1, LED10.cathode
  N12: R7.Pin_1, LED11.cathode
  N13: R8.Pin_1, LED12.cathode
  N14: S1.Pin_2, Bauteil1.D10_PWM/SS, R9.Pin_0
  N15: S1.Pin_3, S1.Pin_4, S2.Pin_3, S2.Pin_4, S3.Pin_3, S3.Pin_4, S4.Pin_4, Bauteil1.5V
  N16: S2.Pin_2, Bauteil1.D11_PWM/MOSI, R10.Pin_0
  N17: S3.Pin_2, Bauteil1.ICSP_MISO, Bauteil1.D12/MISO, R11.Pin_0
  N18: S4.Pin_2, Bauteil1.D13/SCK, R12.Pin_0
  N19: Bauteil1.D2, LED12.anode
  N20: Bauteil1.D3_PWM, LED11.anode
  N21: Bauteil1.D5_PWM, LED10.anode
  N22: Bauteil1.D6_PWM, LED9.anode
